// Logisim project cpu.circ as structural Verilog: 13 circuits, main circuit cpu
module cpu (
);

  wire adder_2_cout, and_1_out, and_2_out, and_3_out, and_4_out, and_5_out, and_6_out, and_7_out, and_8_out,
       and_9_out, CLK_MAIN_out, clock_1_out, clock_2_out, controlled_buffer_1_out, controlled_buffer_2_out,
       controlled_buffer_3_out, controlled_buffer_4_out, controlled_buffer_5_out, controlled_buffer_6_out,
       controlled_buffer_7_out, controlled_buffer_8_out, controlled_buffer_9_out, controlled_buffer_10_out,
       controlled_buffer_11_out, controlled_buffer_12_out, controlled_buffer_13_out,
       controlled_buffer_14_out, controlled_buffer_15_out, controlled_buffer_16_out,
       controlled_buffer_25_out, controlled_buffer_26_out, controlled_buffer_27_out,
       controlled_buffer_28_out, controlled_buffer_29_out, controlled_buffer_30_out,
       controlled_buffer_31_out, controlled_buffer_32_out, controlled_buffer_33_out,
       controlled_buffer_34_out, controlled_buffer_35_out, controlled_buffer_36_out,
       controlled_buffer_37_out, controlled_buffer_38_out, controlled_buffer_39_out,
       controlled_buffer_40_out, controlled_buffer_41_out, controlled_buffer_42_out,
       controlled_buffer_43_out, controlled_buffer_44_out, controlled_buffer_45_out,
       controlled_buffer_46_out, controlled_buffer_47_out, controlled_buffer_48_out,
       instruction_add_1_adda_1, instruction_add_1_adda_2, instruction_add_1_addb_1,
       instruction_add_1_addb_2, instruction_and_or_xor_1_anda_b, instruction_and_or_xor_1_anda_b_2,
       instruction_and_or_xor_1_anda_c, instruction_and_or_xor_1_anda_c_2, instruction_and_or_xor_1_ora_b,
       instruction_and_or_xor_1_ora_b_2, instruction_and_or_xor_1_ora_c, instruction_and_or_xor_1_ora_c_2,
       instruction_and_or_xor_1_xora_b, instruction_and_or_xor_1_xora_b_2, instruction_and_or_xor_1_xora_c,
       instruction_and_or_xor_1_xora_c_2, Instruction_CTR_carry, instruction_jz_jc_jnz_1_jc_1,
       instruction_jz_jc_jnz_1_jc_2, instruction_jz_jc_jnz_1_jc_3, instruction_jz_jc_jnz_1_jc_4,
       instruction_jz_jc_jnz_1_jnz_1, instruction_jz_jc_jnz_1_jnz_2, instruction_jz_jc_jnz_1_jnz_3,
       instruction_jz_jc_jnz_1_jnz_4, instruction_jz_jc_jnz_1_jz_1, instruction_jz_jc_jnz_1_jz_2,
       instruction_jz_jc_jnz_1_jz_3, instruction_jz_jc_jnz_1_jz_4, instruction_lda_sta_1_lda_1,
       instruction_lda_sta_1_lda_2, instruction_lda_sta_1_lda_3, instruction_lda_sta_1_lda_4,
       instruction_lda_sta_1_lda_5, instruction_lda_sta_1_lda_6, instruction_lda_sta_1_sta_1,
       instruction_lda_sta_1_sta_2, instruction_lda_sta_1_sta_3, instruction_lda_sta_1_sta_4,
       instruction_lda_sta_1_sta_5, instruction_lda_sta_1_sta_6, instruction_mov_1_movab_1,
       instruction_mov_1_movab_2, instruction_mov_1_movac_1, instruction_mov_1_movac_2,
       instruction_mov_1_movba_1, instruction_mov_1_movba_2, instruction_mov_1_movbc_1,
       instruction_mov_1_movbc_2, instruction_mov_1_movca_1, instruction_mov_1_movca_2,
       instruction_mov_1_movcb_1, instruction_mov_1_movcb_2, instruction_mvi_1_mvia_1,
       instruction_mvi_1_mvia_2, instruction_mvi_1_mvia_3, instruction_mvi_1_mvia_4, instruction_rst_1_rst_1,
       instruction_sub_1_adda_1, instruction_sub_1_adda_2, instruction_sub_1_addb_1,
       instruction_sub_1_addb_2, intruction_jmp_out_hlt_1_hlt_1, intruction_jmp_out_hlt_1_hlt_2,
       intruction_jmp_out_hlt_1_jmp_1, intruction_jmp_out_hlt_1_jmp_2, intruction_jmp_out_hlt_1_jmp_3,
       intruction_jmp_out_hlt_1_jmp_4, intruction_jmp_out_hlt_1_out_1, intruction_jmp_out_hlt_1_out_2,
       multiplexer_1_out, multiplexer_2_out, not_1_out, not_2_out, not_3_out, not_4_out, not_5_out,
       not_6_out, not_7_out, not_8_out, not_9_out, not_10_out, not_11_out, not_12_out, not_13_out,
       not_14_out, not_15_out, not_16_out, not_17_out, not_18_out, not_19_out, not_20_out, not_21_out,
       not_22_out, not_23_out, not_24_out, not_25_out, not_26_out, not_27_out, not_28_out, or_1_out,
       or_2_out, or_3_out, or_4_out, or_5_out, or_6_out, or_7_out, or_8_out, or_9_out, or_10_out, or_11_out,
       or_12_out, or_13_out, or_14_out, or_19_out, or_20_out, or_21_out, or_25_out, or_34_out,
       pull_resistor_1_node, pull_resistor_3_node, pull_resistor_5_node, pull_resistor_7_node,
       pull_resistor_9_node, pull_resistor_10_node, pull_resistor_13_node, pull_resistor_14_node,
       pull_resistor_16_node, pull_resistor_17_node, pull_resistor_18_node, pull_resistor_19_node,
       pull_resistor_20_node, pull_resistor_21_node, pull_resistor_22_node, pull_resistor_23_node,
       pull_resistor_24_node, pull_resistor_25_node, pull_resistor_28_node, pull_resistor_29_node,
       pull_resistor_30_node, pull_resistor_31_node, pull_resistor_34_node, pull_resistor_35_node,
       RESET_MAIN, undriven;
  wire [1:0] priority_encoder_1_out;
  wire [3:0] adder_1_out, adder_2_out, binary_to_bcd_cvtr_1_out_2, binary_to_bcd_cvtr_1_out_3,
       binary_to_bcd_cvtr_1_out_4, Instruction_CTR_q, xor_4_out, xor_7_out;
  wire [6:3] FLAGS;
  wire [7:0] A_REG, and_11_out, B_REG, C_REG, controlled_buffer_17_out, controlled_buffer_22_out,
       controlled_buffer_23_out, FLAG_REG, INST_REG, MEM_AD_REG, multiplexer_3_out, multiplexer_4_out,
       not_29_out, or_32_out, OUTPUT_REG, PGRM_CTR, ram_1_data, rom_1_data, xor_9_out;
  wire [11:0] controlled_buffer_21_out;

  buf or_1 (or_1_out, intruction_jmp_out_hlt_1_hlt_1);  // OR_Gate
  or or_2 (or_2_out, or_3_out, instruction_lda_sta_1_sta_2, intruction_jmp_out_hlt_1_jmp_2, instruction_lda_sta_1_lda_2, instruction_lda_sta_1_lda_4, and_1_out, instruction_lda_sta_1_sta_4, instruction_mvi_1_mvia_2);
  or or_3 (or_3_out, instruction_jz_jc_jnz_1_jz_2, instruction_jz_jc_jnz_1_jnz_2, instruction_jz_jc_jnz_1_jc_2);
  Clock CLK_MAIN (.out(CLK_MAIN_out));
  Pull_Resistor pull_resistor_1 (.node(pull_resistor_1_node));
  or or_4 (or_4_out, instruction_jz_jc_jnz_1_jz_1, instruction_jz_jc_jnz_1_jnz_1, instruction_jz_jc_jnz_1_jz_3, instruction_jz_jc_jnz_1_jnz_3, instruction_jz_jc_jnz_1_jc_3, instruction_jz_jc_jnz_1_jc_1);
  Multiplexer #(.enable("false")) multiplexer_1 (
    .in0(CLK_MAIN_out), .in1(pull_resistor_1_node), .out(multiplexer_1_out), .sel(or_1_out));
  Pull_Resistor pull_resistor_2 (.node(or_1_out));
  buf or_5 (or_5_out, instruction_lda_sta_1_sta_6);  // OR_Gate
  Instruction_JZ_JC_JNZ instruction_jz_jc_jnz_1 (
    .FLAGS(FLAG_REG), .INPUT(controlled_buffer_21_out), .JZ_1(instruction_jz_jc_jnz_1_jz_1),
    .JZ_2(instruction_jz_jc_jnz_1_jz_2), .JZ_3(instruction_jz_jc_jnz_1_jz_3),
    .JZ_4(instruction_jz_jc_jnz_1_jz_4), .JNZ_1(instruction_jz_jc_jnz_1_jnz_1),
    .JNZ_2(instruction_jz_jc_jnz_1_jnz_2), .JNZ_3(instruction_jz_jc_jnz_1_jnz_3),
    .JNZ_4(instruction_jz_jc_jnz_1_jnz_4), .JC_1(instruction_jz_jc_jnz_1_jc_1),
    .JC_2(instruction_jz_jc_jnz_1_jc_2), .JC_3(instruction_jz_jc_jnz_1_jc_3),
    .JC_4(instruction_jz_jc_jnz_1_jc_4));
  or or_6 (or_6_out, intruction_jmp_out_hlt_1_jmp_4, instruction_lda_sta_1_lda_6, instruction_lda_sta_1_lda_4, or_7_out, instruction_lda_sta_1_sta_4, and_3_out, instruction_mvi_1_mvia_4);
  or or_7 (or_7_out, instruction_jz_jc_jnz_1_jz_4, instruction_jz_jc_jnz_1_jnz_4, instruction_jz_jc_jnz_1_jc_4);
  or or_8 (or_8_out, instruction_jz_jc_jnz_1_jc_2, instruction_jz_jc_jnz_1_jnz_2, instruction_jz_jc_jnz_1_jz_2);
  or or_9 (or_9_out, instruction_jz_jc_jnz_1_jz_4, instruction_jz_jc_jnz_1_jnz_4, instruction_jz_jc_jnz_1_jc_4);
  Instruction_MVI instruction_mvi_1 (
    .INPUT(controlled_buffer_21_out), .MVIA_1(instruction_mvi_1_mvia_1), .MVIA_2(instruction_mvi_1_mvia_2),
    .MVIA_3(instruction_mvi_1_mvia_3), .MVIA_4(instruction_mvi_1_mvia_4));
  buf or_10 (or_10_out, and_3_out);  // OR_Gate
  not not_1 (not_1_out, multiplexer_1_out);
  not not_2 (not_2_out, not_1_out);
  Pull_Resistor pull_resistor_3 (.node(pull_resistor_3_node));
  Multiplexer #(.enable("false")) multiplexer_2 (
    .in0(pull_resistor_3_node), .in1(not_2_out), .out(multiplexer_2_out), .sel(undriven));
  or or_11 (or_11_out, instruction_lda_sta_1_lda_1, instruction_lda_sta_1_sta_1, instruction_lda_sta_1_sta_5, instruction_lda_sta_1_lda_5);
  Instruction_LDA_STA instruction_lda_sta_1 (
    .INPUT(controlled_buffer_21_out), .LDA_1(instruction_lda_sta_1_lda_1),
    .LDA_2(instruction_lda_sta_1_lda_2), .STA_1(instruction_lda_sta_1_sta_1),
    .STA_2(instruction_lda_sta_1_sta_2), .LDA_3(instruction_lda_sta_1_lda_3),
    .LDA_4(instruction_lda_sta_1_lda_4), .STA_3(instruction_lda_sta_1_sta_3),
    .STA_4(instruction_lda_sta_1_sta_4), .LDA_5(instruction_lda_sta_1_lda_5),
    .STA_5(instruction_lda_sta_1_sta_5), .LDA_6(instruction_lda_sta_1_lda_6),
    .STA_6(instruction_lda_sta_1_sta_6));
  Hex_Digit_Display hex_digit_display_1 (.value(A_REG[7:4]));  // open: dp
  Pull_Resistor pull_resistor_4 (.node(or_2_out));
  Pull_Resistor pull_resistor_5 (.node(pull_resistor_5_node));
  Pull_Resistor pull_resistor_6 (.node(or_10_out));
  Pull_Resistor pull_resistor_7 (.node(pull_resistor_7_node));
  not not_3 (not_3_out, Instruction_CTR_q[2]);
  not not_4 (not_4_out, Instruction_CTR_q[3]);
  not not_5 (not_5_out, Instruction_CTR_q[1]);
  and and_1 (and_1_out, not_4_out, not_3_out, not_5_out, not_6_out);
  Hex_Digit_Display hex_digit_display_2 (.value(A_REG[3:0]));  // open: dp
  assign controlled_buffer_1_out = or_2_out ? ram_1_data[2] : 1'bz;  // Controlled_Buffer controlled_buffer_1
  assign controlled_buffer_2_out = or_2_out ? ram_1_data[1] : 1'bz;  // Controlled_Buffer controlled_buffer_2
  assign controlled_buffer_3_out = or_2_out ? ram_1_data[0] : 1'bz;  // Controlled_Buffer controlled_buffer_3
  assign controlled_buffer_4_out = or_10_out ? ram_1_data[2] : 1'bz;  // Controlled_Buffer controlled_buffer_4
  assign controlled_buffer_5_out = or_10_out ? ram_1_data[1] : 1'bz;  // Controlled_Buffer controlled_buffer_5
  assign controlled_buffer_6_out = or_10_out ? ram_1_data[0] : 1'bz;  // Controlled_Buffer controlled_buffer_6
  not not_6 (not_6_out, Instruction_CTR_q[0]);
  not not_7 (not_7_out, Instruction_CTR_q[3]);
  not not_8 (not_8_out, Instruction_CTR_q[2]);
  Hex_Digit_Display hex_digit_display_3 (.value(B_REG[7:4]));  // open: dp
  Hex_Digit_Display hex_digit_display_4 (.value(B_REG[3:0]));  // open: dp
  assign controlled_buffer_7_out = or_2_out ? ram_1_data[4] : 1'bz;  // Controlled_Buffer controlled_buffer_7
  assign controlled_buffer_8_out = or_2_out ? ram_1_data[3] : 1'bz;  // Controlled_Buffer controlled_buffer_8
  assign controlled_buffer_9_out = or_10_out ? ram_1_data[4] : 1'bz;  // Controlled_Buffer controlled_buffer_9
  assign controlled_buffer_10_out = or_10_out ? ram_1_data[3] : 1'bz;  // Controlled_Buffer controlled_buffer_10
  not not_9 (not_9_out, Instruction_CTR_q[1]);
  not not_10 (not_10_out, Instruction_CTR_q[3]);
  and and_2 (and_2_out, not_7_out, not_8_out, not_9_out, Instruction_CTR_q[0]);
  assign controlled_buffer_11_out = or_2_out ? ram_1_data[7] : 1'bz;  // Controlled_Buffer controlled_buffer_11
  assign controlled_buffer_12_out = or_2_out ? ram_1_data[6] : 1'bz;  // Controlled_Buffer controlled_buffer_12
  assign controlled_buffer_13_out = or_2_out ? ram_1_data[5] : 1'bz;  // Controlled_Buffer controlled_buffer_13
  assign controlled_buffer_14_out = or_10_out ? ram_1_data[7] : 1'bz;  // Controlled_Buffer controlled_buffer_14
  assign controlled_buffer_15_out = or_10_out ? ram_1_data[6] : 1'bz;  // Controlled_Buffer controlled_buffer_15
  assign controlled_buffer_16_out = or_10_out ? ram_1_data[5] : 1'bz;  // Controlled_Buffer controlled_buffer_16
  not not_11 (not_11_out, Instruction_CTR_q[3]);
  not not_12 (not_12_out, Instruction_CTR_q[0]);
  not not_13 (not_13_out, Instruction_CTR_q[2]);
  and and_3 (and_3_out, not_10_out, not_13_out, Instruction_CTR_q[1], not_12_out);
  or or_12 (or_12_out, intruction_jmp_out_hlt_1_out_2, intruction_jmp_out_hlt_1_hlt_2, intruction_jmp_out_hlt_1_jmp_1, or_4_out);
  Intruction_JMP_OUT_HLT intruction_jmp_out_hlt_1 (
    .INPUT(controlled_buffer_21_out), .OUT_1(intruction_jmp_out_hlt_1_out_1),
    .OUT_2(intruction_jmp_out_hlt_1_out_2), .HLT_1(intruction_jmp_out_hlt_1_hlt_1),
    .HLT_2(intruction_jmp_out_hlt_1_hlt_2), .JMP_1(intruction_jmp_out_hlt_1_jmp_1),
    .JMP_2(intruction_jmp_out_hlt_1_jmp_2), .JMP_3(intruction_jmp_out_hlt_1_jmp_3),
    .JMP_4(intruction_jmp_out_hlt_1_jmp_4));
  Hex_Digit_Display hex_digit_display_5 (.value(C_REG[7:4]));  // open: dp
  Hex_Digit_Display hex_digit_display_6 (.value(C_REG[3:0]));  // open: dp
  D_Flip_Flop d_ff_1 (
    .D(controlled_buffer_3_out), .clk(multiplexer_1_out), .Q(MEM_AD_REG[0]), .reset(or_34_out));  // open: Qn, preset
  Pull_Resistor pull_resistor_8 (.node(or_6_out));
  Pull_Resistor pull_resistor_9 (.node(pull_resistor_9_node));
  Pull_Resistor pull_resistor_10 (.node(pull_resistor_10_node));
  D_Flip_Flop d_ff_2 (
    .D(controlled_buffer_6_out), .clk(multiplexer_1_out), .Q(INST_REG[0]), .reset(or_34_out));  // open: Qn, preset
  not not_14 (not_14_out, Instruction_CTR_q[2]);
  and and_4 (and_4_out, not_11_out, not_14_out, Instruction_CTR_q[1], Instruction_CTR_q[0]);
  Hex_Digit_Display hex_digit_display_7 (.value(MEM_AD_REG[7:4]));  // open: dp
  D_Flip_Flop d_ff_3 (
    .D(controlled_buffer_2_out), .clk(multiplexer_1_out), .Q(MEM_AD_REG[1]), .reset(or_34_out));  // open: Qn, preset
  Pull_Resistor pull_resistor_11 (.node(or_5_out));
  D_Flip_Flop d_ff_4 (
    .D(controlled_buffer_5_out), .clk(multiplexer_1_out), .Q(INST_REG[1]), .reset(or_34_out));  // open: Qn, preset
  not not_15 (not_15_out, Instruction_CTR_q[1]);
  not not_16 (not_16_out, Instruction_CTR_q[0]);
  not not_17 (not_17_out, Instruction_CTR_q[3]);
  and and_5 (and_5_out, not_17_out, Instruction_CTR_q[2], not_15_out, not_16_out);
  Hex_Digit_Display hex_digit_display_8 (.value(MEM_AD_REG[3:0]));  // open: dp
  D_Flip_Flop d_ff_5 (
    .D(controlled_buffer_1_out), .clk(multiplexer_1_out), .Q(MEM_AD_REG[2]), .reset(or_34_out));  // open: Qn, preset
  RAM ram_1 (.addr(MEM_AD_REG), .we(or_5_out), .oe(or_6_out), .clk(multiplexer_1_out), .data(ram_1_data));
  ROM rom_1 (.addr(controlled_buffer_17_out), .data(rom_1_data));
  assign controlled_buffer_17_out = pull_resistor_10_node ? MEM_AD_REG : 8'bz;  // Controlled_Buffer controlled_buffer_17
  D_Flip_Flop d_ff_6 (
    .D(controlled_buffer_4_out), .clk(multiplexer_1_out), .Q(INST_REG[2]), .reset(or_34_out));  // open: Qn, preset
  Pull_Resistor pull_resistor_12 (.node(multiplexer_2_out));
  Pull_Resistor pull_resistor_13 (.node(pull_resistor_13_node));
  Pull_Resistor #(.pull(1)) pull_resistor_14 (.node(pull_resistor_14_node));
  not not_18 (not_18_out, Instruction_CTR_q[1]);
  not not_19 (not_19_out, Instruction_CTR_q[3]);
  and and_6 (and_6_out, not_19_out, Instruction_CTR_q[2], not_18_out, Instruction_CTR_q[0]);
  Instruction_Add instruction_add_1 (
    .INPUT(controlled_buffer_21_out), .ADDA_1(instruction_add_1_adda_1), .ADDA_2(instruction_add_1_adda_2),
    .ADDB_1(instruction_add_1_addb_1), .ADDB_2(instruction_add_1_addb_2));
  Hex_Digit_Display hex_digit_display_9 (.value(INST_REG[7:4]));  // open: dp
  D_Flip_Flop d_ff_7 (
    .D(controlled_buffer_8_out), .clk(multiplexer_1_out), .Q(MEM_AD_REG[3]), .reset(or_34_out));  // open: Qn, preset
  D_Flip_Flop d_ff_8 (
    .D(controlled_buffer_10_out), .clk(multiplexer_1_out), .Q(INST_REG[3]), .reset(or_34_out));  // open: Qn, preset
  Counter #(.width(4), .max('hf)) Instruction_CTR (
    .clr(multiplexer_2_out), .load(pull_resistor_13_node), .up(pull_resistor_14_node),
    .count(pull_resistor_14_node), .clk(not_1_out), .carry(Instruction_CTR_carry), .Q(Instruction_CTR_q));  // open: D
  not not_20 (not_20_out, Instruction_CTR_q[3]);
  and and_7 (and_7_out, not_20_out, Instruction_CTR_q[2], Instruction_CTR_q[1], not_22_out);
  Instruction_sub instruction_sub_1 (
    .INPUT(controlled_buffer_21_out), .ADDA_1(instruction_sub_1_adda_1), .ADDA_2(instruction_sub_1_adda_2),
    .ADDB_1(instruction_sub_1_addb_1), .ADDB_2(instruction_sub_1_addb_2));
  Hex_Digit_Display hex_digit_display_10 (.value(INST_REG[3:0]));  // open: dp
  D_Flip_Flop d_ff_9 (
    .D(controlled_buffer_7_out), .clk(multiplexer_1_out), .Q(MEM_AD_REG[4]), .reset(or_34_out));  // open: Qn, preset
  D_Flip_Flop d_ff_10 (
    .D(controlled_buffer_9_out), .clk(multiplexer_1_out), .Q(INST_REG[4]), .reset(or_34_out));  // open: Qn, preset
  not not_21 (not_21_out, Instruction_CTR_q[3]);
  not not_22 (not_22_out, Instruction_CTR_q[0]);
  and and_8 (and_8_out, not_21_out, Instruction_CTR_q[2], Instruction_CTR_q[1], Instruction_CTR_q[0]);
  Hex_Digit_Display hex_digit_display_11 (.value(PGRM_CTR[7:4]));  // open: dp
  Hex_Digit_Display hex_digit_display_12 (.value(PGRM_CTR[3:0]));  // open: dp
  D_Flip_Flop d_ff_11 (
    .D(controlled_buffer_13_out), .clk(multiplexer_1_out), .Q(MEM_AD_REG[5]), .reset(or_34_out));  // open: Qn, preset
  D_Flip_Flop d_ff_12 (
    .D(controlled_buffer_16_out), .clk(multiplexer_1_out), .Q(INST_REG[5]), .reset(or_34_out));  // open: Qn, preset
  Pull_Resistor pull_resistor_15 (.node(Instruction_CTR_carry));
  not not_23 (not_23_out, Instruction_CTR_q[1]);
  not not_24 (not_24_out, Instruction_CTR_q[2]);
  and and_9 (and_9_out, Instruction_CTR_q[3], not_24_out, not_23_out, not_25_out);
  Instruction_MOV instruction_mov_1 (
    .INPUT(controlled_buffer_21_out), .MOVAB_1(instruction_mov_1_movab_1),
    .MOVAB_2(instruction_mov_1_movab_2), .MOVAC_1(instruction_mov_1_movac_1),
    .MOVAC_2(instruction_mov_1_movac_2), .MOVBA_1(instruction_mov_1_movba_1),
    .MOVBA_2(instruction_mov_1_movba_2), .MOVBC_1(instruction_mov_1_movbc_1),
    .MOVBC_2(instruction_mov_1_movbc_2), .MOVCA_1(instruction_mov_1_movca_1),
    .MOVCA_2(instruction_mov_1_movca_2), .MOVCB_1(instruction_mov_1_movcb_1),
    .MOVCB_2(instruction_mov_1_movcb_2));
  Hex_Digit_Display hex_digit_display_13 (.value(binary_to_bcd_cvtr_1_out_2));  // open: dp
  D_Flip_Flop d_ff_13 (
    .D(controlled_buffer_12_out), .clk(multiplexer_1_out), .Q(MEM_AD_REG[6]), .reset(or_34_out));  // open: Qn, preset
  assign ram_1_data = pull_resistor_9_node ? rom_1_data : 8'bz;  // Controlled_Buffer controlled_buffer_18
  D_Flip_Flop d_ff_14 (
    .D(controlled_buffer_15_out), .clk(multiplexer_1_out), .Q(INST_REG[6]), .reset(or_34_out));  // open: Qn, preset
  not not_25 (not_25_out, Instruction_CTR_q[0]);
  not not_26 (not_26_out, Instruction_CTR_q[1]);
  not not_27 (not_27_out, Instruction_CTR_q[2]);
  and and_10 (multiplexer_2_out, Instruction_CTR_q[3], not_27_out, not_26_out, Instruction_CTR_q[0]);
  or or_13 (or_13_out, and_9_out, and_8_out, and_7_out, and_6_out, and_5_out, and_4_out, and_3_out);
  or or_14 (or_14_out, instruction_mov_1_movab_2, instruction_mov_1_movac_2, instruction_mov_1_movba_2, instruction_mov_1_movbc_2, instruction_mov_1_movca_2, instruction_mov_1_movcb_2);
  Hex_Digit_Display hex_digit_display_14 (.value(binary_to_bcd_cvtr_1_out_3));  // open: dp
  Binary_to_Bcd_CVTR binary_to_bcd_cvtr_1 (
    .in_1(OUTPUT_REG), .out_2(binary_to_bcd_cvtr_1_out_2), .out_3(binary_to_bcd_cvtr_1_out_3),
    .out_4(binary_to_bcd_cvtr_1_out_4));
  D_Flip_Flop d_ff_15 (
    .D(controlled_buffer_11_out), .clk(multiplexer_1_out), .Q(MEM_AD_REG[7]), .reset(or_34_out));  // open: Qn, preset
  D_Flip_Flop d_ff_16 (
    .D(controlled_buffer_14_out), .clk(multiplexer_1_out), .Q(INST_REG[7]), .reset(or_34_out));  // open: Qn, preset
  Hex_Digit_Display hex_digit_display_15 (.value(binary_to_bcd_cvtr_1_out_4));  // open: dp
  LED led_1 (.in(FLAGS[6]));
  assign ram_1_data = pull_resistor_5_node ? MEM_AD_REG : 8'bz;  // Controlled_Buffer controlled_buffer_19
  assign ram_1_data = pull_resistor_7_node ? INST_REG : 8'bz;  // Controlled_Buffer controlled_buffer_20
  assign controlled_buffer_21_out = or_13_out ? {INST_REG[0], INST_REG[1], INST_REG[2], INST_REG[3], INST_REG[4], INST_REG[5], INST_REG[6], INST_REG[7], Instruction_CTR_q[0], Instruction_CTR_q[1], Instruction_CTR_q[2], Instruction_CTR_q[3]} : 12'bz;  // Controlled_Buffer controlled_buffer_21
  Pull_Resistor pull_resistor_16 (.node(pull_resistor_16_node));
  Button button_1 (.out(RESET_MAIN));
  LED led_2 (.in(FLAGS[3]));
  Pull_Resistor #(.pull(1)) pull_resistor_17 (.node(pull_resistor_17_node));
  not not_28 (not_28_out, FLAGS[3]);
  LED led_3 (.in(not_28_out));
  or or_15 (pull_resistor_16_node, instruction_mvi_1_mvia_1, instruction_add_1_adda_2, instruction_add_1_addb_2, instruction_sub_1_adda_2, instruction_sub_1_addb_2, instruction_and_or_xor_1_xora_b_2, instruction_and_or_xor_1_xora_c_2, instruction_mvi_1_mvia_3, or_11_out, instruction_and_or_xor_1_ora_b_2, or_12_out, instruction_and_or_xor_1_ora_c_2, or_14_out, instruction_and_or_xor_1_anda_c_2, instruction_and_or_xor_1_anda_b_2);
  Pull_Resistor pull_resistor_18 (.node(pull_resistor_18_node));
  Pull_Resistor pull_resistor_19 (.node(pull_resistor_19_node));
  Instruction_AND_OR_XOR instruction_and_or_xor_1 (
    .INPUT(controlled_buffer_21_out), .ANDA_C(instruction_and_or_xor_1_anda_c),
    .ANDA_C_2(instruction_and_or_xor_1_anda_c_2), .ANDA_B(instruction_and_or_xor_1_anda_b),
    .ANDA_B_2(instruction_and_or_xor_1_anda_b_2), .ORA_C(instruction_and_or_xor_1_ora_c),
    .ORA_C_2(instruction_and_or_xor_1_ora_c_2), .ORA_B(instruction_and_or_xor_1_ora_b),
    .ORA_B_2(instruction_and_or_xor_1_ora_b_2), .XORA_C(instruction_and_or_xor_1_xora_c),
    .XORA_C_2(instruction_and_or_xor_1_xora_c_2), .XORA_B(instruction_and_or_xor_1_xora_b),
    .XORA_B_2(instruction_and_or_xor_1_xora_b_2));
  Counter counter_1 (
    .clr(or_34_out), .load(pull_resistor_18_node), .up(pull_resistor_17_node), .count(pull_resistor_16_node),
    .clk(multiplexer_1_out), .D(ram_1_data), .Q(PGRM_CTR));  // open: carry
  or or_16 (pull_resistor_18_node, or_9_out, intruction_jmp_out_hlt_1_jmp_4);
  Pull_Resistor pull_resistor_20 (.node(pull_resistor_20_node));
  assign controlled_buffer_22_out = pull_resistor_20_node ? controlled_buffer_23_out : 8'bz;  // Controlled_Buffer controlled_buffer_22
  Instruction_RST instruction_rst_1 (.INPUT(controlled_buffer_21_out), .RST_1(instruction_rst_1_rst_1));
  assign controlled_buffer_23_out = pull_resistor_20_node ? controlled_buffer_22_out : 8'bz;  // Controlled_Buffer controlled_buffer_23
  buf or_17 (pull_resistor_20_node, instruction_lda_sta_1_lda_4);  // OR_Gate
  assign ram_1_data = pull_resistor_19_node ? PGRM_CTR : 8'bz;  // Controlled_Buffer controlled_buffer_24
  or or_18 (pull_resistor_19_node, or_8_out, and_1_out, instruction_lda_sta_1_sta_2, instruction_lda_sta_1_lda_2, intruction_jmp_out_hlt_1_jmp_2, instruction_mvi_1_mvia_2);
  Pull_Resistor pull_resistor_21 (.node(pull_resistor_21_node));
  Pull_Resistor pull_resistor_22 (.node(pull_resistor_22_node));
  Pull_Resistor pull_resistor_23 (.node(pull_resistor_23_node));
  Pull_Resistor pull_resistor_24 (.node(pull_resistor_24_node));
  Pull_Resistor pull_resistor_25 (.node(pull_resistor_25_node));
  or or_19 (or_19_out, instruction_mov_1_movca_1, instruction_mov_1_movcb_1);
  Priority_Encoder #(.select(2)) priority_encoder_1 (
    .in0(pull_resistor_21_node), .in1(pull_resistor_22_node), .in2(pull_resistor_23_node),
    .in3(pull_resistor_24_node), .out(priority_encoder_1_out));  // open: gs, en_out, en_in
  or or_20 (or_20_out, pull_resistor_21_node, pull_resistor_22_node, pull_resistor_23_node, pull_resistor_24_node);
  or or_21 (or_21_out, instruction_mov_1_movbc_1, instruction_mov_1_movac_1);
  Pull_Resistor pull_resistor_26 (.node(or_19_out));
  Pull_Resistor pull_resistor_27 (.node(or_21_out));
  Pull_Resistor pull_resistor_28 (.node(pull_resistor_28_node));
  Pull_Resistor pull_resistor_29 (.node(pull_resistor_29_node));
  Pull_Resistor pull_resistor_30 (.node(pull_resistor_30_node));
  Pull_Resistor pull_resistor_31 (.node(pull_resistor_31_node));
  not not_29 (not_29_out[0], not_29_out[6]);
  or or_22 (pull_resistor_28_node, instruction_mov_1_movbc_1, instruction_mov_1_movba_1);
  assign controlled_buffer_25_out = or_19_out ? ram_1_data[2] : 1'bz;  // Controlled_Buffer controlled_buffer_25
  assign controlled_buffer_26_out = or_19_out ? ram_1_data[1] : 1'bz;  // Controlled_Buffer controlled_buffer_26
  assign controlled_buffer_27_out = or_19_out ? ram_1_data[0] : 1'bz;  // Controlled_Buffer controlled_buffer_27
  assign controlled_buffer_28_out = pull_resistor_28_node ? ram_1_data[2] : 1'bz;  // Controlled_Buffer controlled_buffer_28
  assign controlled_buffer_29_out = pull_resistor_28_node ? ram_1_data[1] : 1'bz;  // Controlled_Buffer controlled_buffer_29
  assign controlled_buffer_30_out = pull_resistor_28_node ? ram_1_data[0] : 1'bz;  // Controlled_Buffer controlled_buffer_30
  assign controlled_buffer_31_out = pull_resistor_30_node ? ram_1_data[1] : 1'bz;  // Controlled_Buffer controlled_buffer_31
  assign controlled_buffer_32_out = pull_resistor_30_node ? ram_1_data[0] : 1'bz;  // Controlled_Buffer controlled_buffer_32
  xor xor_1 (xor_4_out[3], A_REG[7], pull_resistor_25_node);
  or or_23 (pull_resistor_29_node, instruction_mov_1_movcb_1, instruction_mov_1_movab_1);
  assign controlled_buffer_33_out = or_19_out ? ram_1_data[4] : 1'bz;  // Controlled_Buffer controlled_buffer_33
  assign controlled_buffer_34_out = or_19_out ? ram_1_data[3] : 1'bz;  // Controlled_Buffer controlled_buffer_34
  assign controlled_buffer_35_out = pull_resistor_28_node ? ram_1_data[4] : 1'bz;  // Controlled_Buffer controlled_buffer_35
  assign controlled_buffer_36_out = pull_resistor_28_node ? ram_1_data[3] : 1'bz;  // Controlled_Buffer controlled_buffer_36
  assign controlled_buffer_37_out = pull_resistor_30_node ? ram_1_data[4] : 1'bz;  // Controlled_Buffer controlled_buffer_37
  assign controlled_buffer_38_out = pull_resistor_30_node ? ram_1_data[3] : 1'bz;  // Controlled_Buffer controlled_buffer_38
  assign controlled_buffer_39_out = pull_resistor_30_node ? ram_1_data[2] : 1'bz;  // Controlled_Buffer controlled_buffer_39
  xor xor_2 (xor_4_out[1], A_REG[5], pull_resistor_25_node);
  xor xor_3 (xor_4_out[2], A_REG[6], pull_resistor_25_node);
  or or_24 (pull_resistor_30_node, instruction_mov_1_movab_1, instruction_add_1_adda_1, instruction_add_1_addb_1, instruction_sub_1_adda_1, instruction_sub_1_addb_1, instruction_and_or_xor_1_anda_c, instruction_mov_1_movac_1, instruction_and_or_xor_1_anda_b, instruction_and_or_xor_1_ora_c, instruction_and_or_xor_1_ora_b, instruction_and_or_xor_1_xora_c, instruction_and_or_xor_1_xora_b, or_25_out);
  assign controlled_buffer_40_out = or_19_out ? ram_1_data[7] : 1'bz;  // Controlled_Buffer controlled_buffer_40
  assign controlled_buffer_41_out = or_19_out ? ram_1_data[6] : 1'bz;  // Controlled_Buffer controlled_buffer_41
  assign controlled_buffer_42_out = or_19_out ? ram_1_data[5] : 1'bz;  // Controlled_Buffer controlled_buffer_42
  assign controlled_buffer_43_out = pull_resistor_28_node ? ram_1_data[7] : 1'bz;  // Controlled_Buffer controlled_buffer_43
  assign controlled_buffer_44_out = pull_resistor_28_node ? ram_1_data[6] : 1'bz;  // Controlled_Buffer controlled_buffer_44
  assign controlled_buffer_45_out = pull_resistor_28_node ? ram_1_data[5] : 1'bz;  // Controlled_Buffer controlled_buffer_45
  assign controlled_buffer_46_out = pull_resistor_30_node ? ram_1_data[7] : 1'bz;  // Controlled_Buffer controlled_buffer_46
  assign controlled_buffer_47_out = pull_resistor_30_node ? ram_1_data[6] : 1'bz;  // Controlled_Buffer controlled_buffer_47
  assign controlled_buffer_48_out = pull_resistor_30_node ? ram_1_data[5] : 1'bz;  // Controlled_Buffer controlled_buffer_48
  xor xor_4 (xor_4_out[0], A_REG[4], pull_resistor_25_node);
  or or_25 (or_25_out, instruction_mvi_1_mvia_4, instruction_lda_sta_1_lda_6);
  D_Flip_Flop d_ff_17 (
    .D(controlled_buffer_27_out), .clk(multiplexer_1_out), .Q(C_REG[0]), .reset(or_34_out));  // open: Qn, preset
  D_Flip_Flop d_ff_18 (
    .D(controlled_buffer_30_out), .clk(multiplexer_1_out), .Q(B_REG[0]), .reset(or_34_out));  // open: Qn, preset
  D_Flip_Flop d_ff_19 (
    .D(controlled_buffer_32_out), .clk(multiplexer_1_out), .Q(A_REG[0]), .reset(or_34_out));  // open: Qn, preset
  xor xor_5 (xor_7_out[3], A_REG[3], pull_resistor_25_node);
  Adder #(.width(4)) adder_1 (
    .a(xor_4_out), .b(multiplexer_4_out[7:4]), .out(adder_1_out), .cin(adder_2_cout), .cout(not_29_out[6]));
  or or_26 (pull_resistor_25_node, instruction_sub_1_adda_1, instruction_sub_1_addb_1);
  or or_27 (pull_resistor_31_node, instruction_mov_1_movba_1, intruction_jmp_out_hlt_1_out_1, instruction_lda_sta_1_sta_6, instruction_mov_1_movca_1);
  D_Flip_Flop d_ff_20 (
    .D(controlled_buffer_26_out), .clk(multiplexer_1_out), .Q(C_REG[1]), .reset(or_34_out));  // open: Qn, preset
  D_Flip_Flop d_ff_21 (
    .D(controlled_buffer_29_out), .clk(multiplexer_1_out), .Q(B_REG[1]), .reset(or_34_out));  // open: Qn, preset
  D_Flip_Flop d_ff_22 (
    .D(controlled_buffer_31_out), .clk(multiplexer_1_out), .Q(A_REG[1]), .reset(or_34_out));  // open: Qn, preset
  xor xor_6 (xor_7_out[2], A_REG[2], pull_resistor_25_node);
  Adder #(.width(4)) adder_2 (
    .a(xor_7_out), .b(multiplexer_4_out[3:0]), .out(adder_2_out), .cin(pull_resistor_25_node),
    .cout(adder_2_cout));
  or or_28 (pull_resistor_21_node, instruction_add_1_adda_1, instruction_sub_1_adda_1, instruction_sub_1_addb_1, instruction_add_1_addb_1);
  D_Flip_Flop d_ff_23 (
    .D(controlled_buffer_25_out), .clk(multiplexer_1_out), .Q(C_REG[2]), .reset(or_34_out));  // open: Qn, preset
  D_Flip_Flop d_ff_24 (
    .D(controlled_buffer_28_out), .clk(multiplexer_1_out), .Q(B_REG[2]), .reset(or_34_out));  // open: Qn, preset
  D_Flip_Flop d_ff_25 (
    .D(controlled_buffer_39_out), .clk(multiplexer_1_out), .Q(A_REG[2]), .reset(or_34_out));  // open: Qn, preset
  xor xor_7 (xor_7_out[0], A_REG[0], pull_resistor_25_node);
  xor xor_8 (xor_7_out[1], A_REG[1], pull_resistor_25_node);
  or or_29 (pull_resistor_22_node, instruction_and_or_xor_1_anda_c, instruction_and_or_xor_1_anda_b);
  D_Flip_Flop d_ff_26 (
    .D(controlled_buffer_34_out), .clk(multiplexer_1_out), .Q(C_REG[3]), .reset(or_34_out));  // open: Qn, preset
  D_Flip_Flop d_ff_27 (
    .D(controlled_buffer_36_out), .clk(multiplexer_1_out), .Q(B_REG[3]), .reset(or_34_out));  // open: Qn, preset
  D_Flip_Flop d_ff_28 (
    .D(controlled_buffer_38_out), .clk(multiplexer_1_out), .Q(A_REG[3]), .reset(or_34_out));  // open: Qn, preset
  or or_30 (pull_resistor_24_node, instruction_and_or_xor_1_xora_c, instruction_and_or_xor_1_xora_b);
  or or_31 (pull_resistor_23_node, instruction_and_or_xor_1_ora_c, instruction_and_or_xor_1_ora_b);
  D_Flip_Flop d_ff_29 (
    .D(controlled_buffer_33_out), .clk(multiplexer_1_out), .Q(C_REG[4]), .reset(or_34_out));  // open: Qn, preset
  D_Flip_Flop d_ff_30 (
    .D(controlled_buffer_35_out), .clk(multiplexer_1_out), .Q(B_REG[4]), .reset(or_34_out));  // open: Qn, preset
  D_Flip_Flop d_ff_31 (
    .D(controlled_buffer_37_out), .clk(multiplexer_1_out), .Q(A_REG[4]), .reset(or_34_out));  // open: Qn, preset
  assign and_11_out = multiplexer_4_out & A_REG;  // AND_Gate and_11, 8 bits wide
  D_Flip_Flop d_ff_32 (
    .D(controlled_buffer_42_out), .clk(multiplexer_1_out), .Q(C_REG[5]), .reset(or_34_out));  // open: Qn, preset
  D_Flip_Flop d_ff_33 (
    .D(controlled_buffer_45_out), .clk(multiplexer_1_out), .Q(B_REG[5]), .reset(or_34_out));  // open: Qn, preset
  D_Flip_Flop d_ff_34 (
    .D(controlled_buffer_48_out), .clk(multiplexer_1_out), .Q(A_REG[5]), .reset(or_34_out));  // open: Qn, preset
  assign or_32_out = multiplexer_4_out | A_REG;  // OR_Gate or_32, 8 bits wide
  D_Flip_Flop d_ff_35 (
    .D(controlled_buffer_41_out), .clk(multiplexer_1_out), .Q(C_REG[6]), .reset(or_34_out));  // open: Qn, preset
  D_Flip_Flop d_ff_36 (
    .D(controlled_buffer_44_out), .clk(multiplexer_1_out), .Q(B_REG[6]), .reset(or_34_out));  // open: Qn, preset
  D_Flip_Flop d_ff_37 (
    .D(controlled_buffer_47_out), .clk(multiplexer_1_out), .Q(A_REG[6]), .reset(or_34_out));  // open: Qn, preset
  assign xor_9_out = multiplexer_4_out ^ A_REG;  // XOR_Gate xor_9, 8 bits wide
  D_Flip_Flop d_ff_38 (
    .D(controlled_buffer_40_out), .clk(multiplexer_1_out), .Q(C_REG[7]), .reset(or_34_out));  // open: Qn, preset
  D_Flip_Flop d_ff_39 (
    .D(controlled_buffer_43_out), .clk(multiplexer_1_out), .Q(B_REG[7]), .reset(or_34_out));  // open: Qn, preset
  D_Flip_Flop d_ff_40 (
    .D(controlled_buffer_46_out), .clk(multiplexer_1_out), .Q(A_REG[7]), .reset(or_34_out));  // open: Qn, preset
  Pull_Resistor pull_resistor_32 (.node(not_29_out[7]));
  Multiplexer #(.select(2), .width(8)) multiplexer_3 (
    .in0({adder_1_out, adder_2_out}), .in1(and_11_out), .in2(or_32_out), .in3(xor_9_out),
    .out(multiplexer_3_out), .sel(priority_encoder_1_out), .en(or_20_out));
  Register register_1 (
    .D(ram_1_data), .en(intruction_jmp_out_hlt_1_out_1), .clk(clock_1_out), .Q(OUTPUT_REG), .clr(or_34_out));
  Pull_Resistor pull_resistor_33 (.node(intruction_jmp_out_hlt_1_out_1));
  Clock clock_1 (.out(clock_1_out));
  assign ram_1_data = or_21_out ? C_REG : 8'bz;  // Controlled_Buffer controlled_buffer_49
  assign ram_1_data = pull_resistor_29_node ? B_REG : 8'bz;  // Controlled_Buffer controlled_buffer_50
  assign ram_1_data = pull_resistor_31_node ? A_REG : 8'bz;  // Controlled_Buffer controlled_buffer_51
  Clock clock_2 (.out(clock_2_out));
  nor nor_1 (not_29_out[3], multiplexer_3_out[0], multiplexer_3_out[1], multiplexer_3_out[2], multiplexer_3_out[3], multiplexer_3_out[4], multiplexer_3_out[5], multiplexer_3_out[6], multiplexer_3_out[7]);
  Register Flag_Register (
    .D({not_29_out[7:6], {2{not_29_out[7]}}, not_29_out[3], {2{not_29_out[7]}}, not_29_out[0]}),
    .en(or_20_out), .clk(clock_2_out), .Q(FLAG_REG), .clr(or_34_out));
  assign ram_1_data = or_20_out ? multiplexer_3_out : 8'bz;  // Controlled_Buffer controlled_buffer_52
  assign ram_1_data = pull_resistor_34_node ? FLAG_REG : 8'bz;  // Controlled_Buffer controlled_buffer_53
  Pull_Resistor pull_resistor_34 (.node(pull_resistor_34_node));
  Pull_Resistor pull_resistor_35 (.node(pull_resistor_35_node));
  Multiplexer #(.width(8), .enable("false")) multiplexer_4 (
    .in0(B_REG), .in1(C_REG), .out(multiplexer_4_out), .sel(pull_resistor_35_node));
  or or_33 (pull_resistor_35_node, instruction_add_1_addb_1, instruction_sub_1_addb_1, instruction_and_or_xor_1_anda_b, instruction_and_or_xor_1_ora_b, instruction_and_or_xor_1_xora_b);
  or or_34 (or_34_out, instruction_rst_1_rst_1, RESET_MAIN);

  // Notes on the sheet:
  //   HLT
  //   MARI
  //   MARO
  //   RAMIN
  //   RAMOUT
  //   ROMAD
  //   ROMOUT
  //   IROUT
  //   IRIN
  //   CARRY
  //   ZERO
  //   POSITIVE
  //   CTREN
  //   CTRIN
  //   ALE
  //   CTROUT
  //   CIN
  //   COUT
  //   BIN
  //   BOUT
  //   AIN
  //   AOUT
  //   SUB
  //   SUM
  //   AND
  //   OR
  //   XOR
  //   REG C SELECT
endmodule

module alu (
  input  [7:0] in_1,
  input  [7:0] in_2
);

  wire adder_1_cout, adder_2_cout, and_2_out, clock_1_out, controlled_buffer_1_out, controlled_buffer_2_out,
       controlled_buffer_3_out, controlled_buffer_4_out, controlled_buffer_5_out, controlled_buffer_6_out,
       controlled_buffer_7_out, controlled_buffer_8_out, not_1_out, not_2_out, or_1_out, undriven, undriven_2;
  wire [1:0] priority_encoder_1_out;
  wire [3:0] xor_1_out, xor_8_out;
  wire [7:0] adder_2_out, and_1_out, controlled_buffer_9_out, controlled_buffer_10_out, d_ff_1_q,
       multiplexer_1_out, or_2_out, xor_9_out;

  Priority_Encoder #(.select(2)) priority_encoder_1 (
    .in0(1'b1), .in1(1'b0), .in2(1'b0), .in3(1'b0), .out(priority_encoder_1_out));  // open: gs, en_out, en_in
  Clock clock_1 (.out(clock_1_out));
  not not_1 (not_1_out, adder_1_cout);
  or or_1 (or_1_out, 1'b1, 1'b0, 1'b0, 1'b0);
  xor xor_1 (xor_1_out[0], in_1[7], 1'b0);
  assign controlled_buffer_1_out = or_1_out ? controlled_buffer_10_out[2] : 1'bz;  // Controlled_Buffer controlled_buffer_1
  assign controlled_buffer_2_out = or_1_out ? controlled_buffer_10_out[1] : 1'bz;  // Controlled_Buffer controlled_buffer_2
  assign controlled_buffer_3_out = or_1_out ? controlled_buffer_10_out[0] : 1'bz;  // Controlled_Buffer controlled_buffer_3
  xor xor_2 (xor_1_out[1], in_1[6], 1'b0);
  assign controlled_buffer_4_out = or_1_out ? controlled_buffer_10_out[5] : 1'bz;  // Controlled_Buffer controlled_buffer_4
  assign controlled_buffer_5_out = or_1_out ? controlled_buffer_10_out[4] : 1'bz;  // Controlled_Buffer controlled_buffer_5
  assign controlled_buffer_6_out = or_1_out ? controlled_buffer_10_out[3] : 1'bz;  // Controlled_Buffer controlled_buffer_6
  xor xor_3 (xor_1_out[3], in_1[4], 1'b0);
  xor xor_4 (xor_1_out[2], in_1[5], 1'b0);
  assign controlled_buffer_7_out = or_1_out ? controlled_buffer_10_out[7] : 1'bz;  // Controlled_Buffer controlled_buffer_7
  assign controlled_buffer_8_out = or_1_out ? controlled_buffer_10_out[6] : 1'bz;  // Controlled_Buffer controlled_buffer_8
  xor xor_5 (xor_8_out[3], in_1[3], 1'b0);
  Adder #(.width(4)) adder_1 (
    .a(xor_1_out), .b(in_2[7:4]), .out(adder_2_out[7:4]), .cin(adder_2_cout), .cout(adder_1_cout));
  D_Flip_Flop d_ff_1 (
    .D(controlled_buffer_3_out), .clk(clock_1_out), .Q(d_ff_1_q[0]), .reset(undriven_2));  // open: Qn, preset
  xor xor_6 (xor_8_out[2], in_1[2], 1'b0);
  Adder #(.width(4)) adder_2 (.a(xor_8_out), .b(in_2[3:0]), .out(adder_2_out[3:0]), .cin(1'b0), .cout(adder_2_cout));
  D_Flip_Flop d_ff_2 (
    .D(controlled_buffer_2_out), .clk(clock_1_out), .Q(d_ff_1_q[1]), .reset(undriven_2));  // open: Qn, preset
  xor xor_7 (xor_8_out[1], in_1[1], 1'b0);
  not not_2 (not_2_out, and_2_out);
  D_Flip_Flop d_ff_3 (
    .D(controlled_buffer_1_out), .clk(clock_1_out), .Q(d_ff_1_q[2]), .reset(undriven_2));  // open: Qn, preset
  xor xor_8 (xor_8_out[0], in_1[0], 1'b0);
  D_Flip_Flop d_ff_4 (
    .D(controlled_buffer_6_out), .clk(clock_1_out), .Q(d_ff_1_q[3]), .reset(undriven_2));  // open: Qn, preset
  assign and_1_out = in_2 & in_1;  // AND_Gate and_1, 8 bits wide
  D_Flip_Flop d_ff_5 (
    .D(controlled_buffer_5_out), .clk(clock_1_out), .Q(d_ff_1_q[4]), .reset(undriven_2));  // open: Qn, preset
  assign or_2_out = in_2 | in_1;  // OR_Gate or_2, 8 bits wide
  D_Flip_Flop d_ff_6 (
    .D(controlled_buffer_4_out), .clk(clock_1_out), .Q(d_ff_1_q[5]), .reset(undriven_2));  // open: Qn, preset
  assign xor_9_out = in_2 ^ in_1;  // XOR_Gate xor_9, 8 bits wide
  D_Flip_Flop d_ff_7 (
    .D(controlled_buffer_8_out), .clk(clock_1_out), .Q(d_ff_1_q[6]), .reset(undriven_2));  // open: Qn, preset
  Multiplexer #(.select(2), .width(8)) multiplexer_1 (
    .in0(adder_2_out), .in1(and_1_out), .in2(or_2_out), .in3(xor_9_out), .out(multiplexer_1_out),
    .sel(priority_encoder_1_out), .en(or_1_out));
  D_Flip_Flop d_ff_8 (
    .D(controlled_buffer_7_out), .clk(clock_1_out), .Q(d_ff_1_q[7]), .reset(undriven_2));  // open: Qn, preset
  and and_2 (and_2_out, multiplexer_1_out[0], multiplexer_1_out[1], multiplexer_1_out[2], multiplexer_1_out[3], multiplexer_1_out[4], multiplexer_1_out[5], multiplexer_1_out[6], multiplexer_1_out[7]);
  assign controlled_buffer_9_out = undriven ? d_ff_1_q : 8'bz;  // Controlled_Buffer controlled_buffer_9
  assign controlled_buffer_10_out = or_1_out ? multiplexer_1_out : 8'bz;  // Controlled_Buffer controlled_buffer_10
endmodule

module test (
  input  in_1,
  input  in_2,
  input  in_3,
  input  in_4,
  output out_5,
  output out_6,
  output out_7,
  output out_8
);

  wire and_1_out, and_2_out;
  wire [3:1] or_1_out;

  and and_1 (and_1_out, in_3, in_1);
  and and_2 (and_2_out, in_3, in_2);
  or or_1 (or_1_out[1], and_2_out, and_1_out, in_4);
  Pull_Resistor pull_resistor_1 (.node(or_1_out[3]));
  Adder #(.width(4)) adder_1 (
    .a({in_4, in_3, in_2, in_1}), .b({{2{or_1_out[3]}}, {2{or_1_out[1]}}}), .out({out_5, out_6, out_7, out_8}));  // open: cin, cout
  // OR_Gate or_2 is placed but not wired
endmodule

module Instruction_Add (
  input  [11:0] INPUT,
  output ADDA_1,
  output ADDA_2,
  output ADDB_1,
  output ADDB_2
);

  wire not_1_out, not_2_out, not_3_out, not_4_out, not_5_out, not_6_out, not_7_out, not_8_out, not_9_out,
       not_10_out, not_11_out, not_12_out, not_13_out, not_14_out, not_15_out, not_16_out, not_17_out,
       not_18_out, not_19_out, not_20_out;

  not not_1 (not_1_out, INPUT[0]);
  not not_2 (not_2_out, INPUT[1]);
  not not_3 (not_3_out, INPUT[5]);
  not not_4 (not_4_out, INPUT[6]);
  not not_5 (not_5_out, INPUT[7]);
  not not_6 (not_6_out, INPUT[0]);
  not not_7 (not_7_out, INPUT[2]);
  not not_8 (not_8_out, INPUT[3]);
  not not_9 (not_9_out, INPUT[5]);
  not not_10 (not_10_out, INPUT[6]);
  not not_11 (not_11_out, INPUT[7]);
  not not_12 (not_12_out, INPUT[0]);
  not not_13 (not_13_out, INPUT[1]);
  not not_14 (not_14_out, INPUT[5]);
  not not_15 (not_15_out, INPUT[6]);
  not not_16 (not_16_out, INPUT[0]);
  not not_17 (not_17_out, INPUT[2]);
  not not_18 (not_18_out, INPUT[3]);
  not not_19 (not_19_out, INPUT[5]);
  not not_20 (not_20_out, INPUT[6]);
  and and_1 (ADDA_1, not_1_out, not_2_out, INPUT[2], INPUT[3], INPUT[4], not_3_out, not_4_out, not_5_out, INPUT[8], INPUT[9], INPUT[10], INPUT[11]);
  and and_2 (ADDA_2, not_6_out, INPUT[1], not_7_out, not_8_out, INPUT[4], not_9_out, not_10_out, not_11_out, INPUT[8], INPUT[9], INPUT[10], INPUT[11]);
  and and_3 (ADDB_1, not_12_out, not_13_out, INPUT[2], INPUT[3], INPUT[4], not_14_out, not_15_out, INPUT[7], INPUT[8], INPUT[9], INPUT[10], INPUT[11]);
  and and_4 (ADDB_2, not_16_out, INPUT[1], not_17_out, not_18_out, INPUT[4], not_19_out, not_20_out, INPUT[7], INPUT[8], INPUT[9], INPUT[10], INPUT[11]);
endmodule

module Instruction_MOV (
  input  [11:0] INPUT,
  output MOVAB_1,
  output MOVAB_2,
  output MOVAC_1,
  output MOVAC_2,
  output MOVBA_1,
  output MOVBA_2,
  output MOVBC_1,
  output MOVBC_2,
  output MOVCA_1,
  output MOVCA_2,
  output MOVCB_1,
  output MOVCB_2
);

  wire not_1_out, not_2_out, not_3_out, not_4_out, not_5_out, not_6_out, not_7_out, not_8_out, not_9_out,
       not_10_out, not_11_out, not_12_out, not_13_out, not_14_out, not_15_out, not_16_out, not_17_out,
       not_18_out, not_19_out, not_20_out, not_21_out, not_22_out, not_23_out, not_24_out, not_25_out,
       not_26_out, not_27_out, not_28_out, not_29_out, not_30_out, not_31_out, not_32_out, not_33_out,
       not_34_out, not_35_out, not_36_out, not_37_out, not_38_out, not_39_out, not_40_out, not_41_out,
       not_42_out, not_43_out, not_44_out, not_45_out, not_46_out, not_47_out, not_48_out, not_49_out,
       not_50_out, not_51_out, not_52_out, not_53_out, not_54_out, not_55_out, not_56_out, not_57_out,
       not_58_out, not_59_out, not_60_out, not_61_out, not_62_out, not_63_out, not_64_out, not_65_out,
       not_66_out, not_67_out, not_68_out, not_69_out, not_70_out, not_71_out, not_72_out, not_73_out,
       not_74_out, not_75_out, not_76_out, not_77_out, not_78_out, not_79_out, not_80_out, not_81_out,
       not_82_out, not_83_out, not_84_out, not_85_out, not_86_out, not_87_out, not_88_out, not_89_out,
       not_90_out, not_91_out, not_92_out, not_93_out, not_94_out, not_95_out, not_96_out, not_97_out,
       not_98_out, not_99_out, not_100_out, not_101_out, not_102_out, not_103_out, not_104_out, not_105_out,
       not_106_out, not_107_out, not_108_out;

  not not_1 (not_1_out, INPUT[0]);
  not not_2 (not_2_out, INPUT[1]);
  not not_3 (not_3_out, INPUT[4]);
  not not_4 (not_4_out, INPUT[5]);
  not not_5 (not_5_out, INPUT[6]);
  not not_6 (not_6_out, INPUT[7]);
  not not_7 (not_7_out, INPUT[8]);
  not not_8 (not_8_out, INPUT[9]);
  not not_9 (not_9_out, INPUT[10]);
  not not_10 (not_10_out, INPUT[0]);
  not not_11 (not_11_out, INPUT[2]);
  not not_12 (not_12_out, INPUT[3]);
  not not_13 (not_13_out, INPUT[4]);
  not not_14 (not_14_out, INPUT[5]);
  not not_15 (not_15_out, INPUT[6]);
  not not_16 (not_16_out, INPUT[7]);
  not not_17 (not_17_out, INPUT[8]);
  not not_18 (not_18_out, INPUT[9]);
  not not_19 (not_19_out, INPUT[10]);
  not not_20 (not_20_out, INPUT[0]);
  not not_21 (not_21_out, INPUT[1]);
  not not_22 (not_22_out, INPUT[4]);
  not not_23 (not_23_out, INPUT[5]);
  not not_24 (not_24_out, INPUT[6]);
  not not_25 (not_25_out, INPUT[7]);
  not not_26 (not_26_out, INPUT[8]);
  not not_27 (not_27_out, INPUT[9]);
  not not_28 (not_28_out, INPUT[11]);
  not not_29 (not_29_out, INPUT[0]);
  not not_30 (not_30_out, INPUT[2]);
  not not_31 (not_31_out, INPUT[3]);
  not not_32 (not_32_out, INPUT[4]);
  not not_33 (not_33_out, INPUT[5]);
  not not_34 (not_34_out, INPUT[6]);
  not not_35 (not_35_out, INPUT[7]);
  not not_36 (not_36_out, INPUT[8]);
  not not_37 (not_37_out, INPUT[9]);
  not not_38 (not_38_out, INPUT[11]);
  not not_39 (not_39_out, INPUT[0]);
  not not_40 (not_40_out, INPUT[1]);
  not not_41 (not_41_out, INPUT[4]);
  not not_42 (not_42_out, INPUT[5]);
  not not_43 (not_43_out, INPUT[6]);
  not not_44 (not_44_out, INPUT[7]);
  not not_45 (not_45_out, INPUT[8]);
  not not_46 (not_46_out, INPUT[9]);
  not not_47 (not_47_out, INPUT[0]);
  not not_48 (not_48_out, INPUT[2]);
  not not_49 (not_49_out, INPUT[3]);
  not not_50 (not_50_out, INPUT[4]);
  not not_51 (not_51_out, INPUT[5]);
  not not_52 (not_52_out, INPUT[6]);
  not not_53 (not_53_out, INPUT[7]);
  not not_54 (not_54_out, INPUT[8]);
  not not_55 (not_55_out, INPUT[9]);
  not not_56 (not_56_out, INPUT[0]);
  not not_57 (not_57_out, INPUT[1]);
  not not_58 (not_58_out, INPUT[4]);
  not not_59 (not_59_out, INPUT[5]);
  not not_60 (not_60_out, INPUT[6]);
  not not_61 (not_61_out, INPUT[7]);
  not not_62 (not_62_out, INPUT[8]);
  not not_63 (not_63_out, INPUT[10]);
  not not_64 (not_64_out, INPUT[11]);
  not not_65 (not_65_out, INPUT[0]);
  not not_66 (not_66_out, INPUT[2]);
  not not_67 (not_67_out, INPUT[3]);
  not not_68 (not_68_out, INPUT[4]);
  not not_69 (not_69_out, INPUT[5]);
  not not_70 (not_70_out, INPUT[6]);
  not not_71 (not_71_out, INPUT[7]);
  not not_72 (not_72_out, INPUT[8]);
  not not_73 (not_73_out, INPUT[10]);
  not not_74 (not_74_out, INPUT[11]);
  not not_75 (not_75_out, INPUT[0]);
  not not_76 (not_76_out, INPUT[1]);
  not not_77 (not_77_out, INPUT[4]);
  not not_78 (not_78_out, INPUT[5]);
  not not_79 (not_79_out, INPUT[6]);
  not not_80 (not_80_out, INPUT[7]);
  not not_81 (not_81_out, INPUT[8]);
  not not_82 (not_82_out, INPUT[10]);
  not not_83 (not_83_out, INPUT[0]);
  not not_84 (not_84_out, INPUT[2]);
  not not_85 (not_85_out, INPUT[3]);
  not not_86 (not_86_out, INPUT[4]);
  not not_87 (not_87_out, INPUT[5]);
  not not_88 (not_88_out, INPUT[6]);
  not not_89 (not_89_out, INPUT[7]);
  not not_90 (not_90_out, INPUT[8]);
  not not_91 (not_91_out, INPUT[10]);
  not not_92 (not_92_out, INPUT[0]);
  not not_93 (not_93_out, INPUT[1]);
  not not_94 (not_94_out, INPUT[4]);
  not not_95 (not_95_out, INPUT[5]);
  not not_96 (not_96_out, INPUT[6]);
  not not_97 (not_97_out, INPUT[7]);
  not not_98 (not_98_out, INPUT[8]);
  not not_99 (not_99_out, INPUT[11]);
  not not_100 (not_100_out, INPUT[0]);
  not not_101 (not_101_out, INPUT[2]);
  not not_102 (not_102_out, INPUT[3]);
  not not_103 (not_103_out, INPUT[4]);
  not not_104 (not_104_out, INPUT[5]);
  not not_105 (not_105_out, INPUT[6]);
  not not_106 (not_106_out, INPUT[7]);
  not not_107 (not_107_out, INPUT[8]);
  not not_108 (not_108_out, INPUT[11]);
  and and_1 (MOVAB_1, not_1_out, not_2_out, INPUT[2], INPUT[3], not_3_out, not_4_out, not_5_out, not_6_out, not_7_out, not_8_out, not_9_out, INPUT[11]);
  and and_2 (MOVAB_2, not_10_out, INPUT[1], not_11_out, not_12_out, not_13_out, not_14_out, not_15_out, not_16_out, not_17_out, not_18_out, not_19_out, INPUT[11]);
  and and_3 (MOVAC_1, not_20_out, not_21_out, INPUT[2], INPUT[3], not_22_out, not_23_out, not_24_out, not_25_out, not_26_out, not_27_out, INPUT[10], not_28_out);
  and and_4 (MOVAC_2, not_29_out, INPUT[1], not_30_out, not_31_out, not_32_out, not_33_out, not_34_out, not_35_out, not_36_out, not_37_out, INPUT[10], not_38_out);
  and and_5 (MOVBA_1, not_39_out, not_40_out, INPUT[2], INPUT[3], not_41_out, not_42_out, not_43_out, not_44_out, not_45_out, not_46_out, INPUT[10], INPUT[11]);
  and and_6 (MOVBA_2, not_47_out, INPUT[1], not_48_out, not_49_out, not_50_out, not_51_out, not_52_out, not_53_out, not_54_out, not_55_out, INPUT[10], INPUT[11]);
  and and_7 (MOVBC_1, not_56_out, not_57_out, INPUT[2], INPUT[3], not_58_out, not_59_out, not_60_out, not_61_out, not_62_out, INPUT[9], not_63_out, not_64_out);
  and and_8 (MOVBC_2, not_65_out, INPUT[1], not_66_out, not_67_out, not_68_out, not_69_out, not_70_out, not_71_out, not_72_out, INPUT[9], not_73_out, not_74_out);
  and and_9 (MOVCA_1, not_75_out, not_76_out, INPUT[2], INPUT[3], not_77_out, not_78_out, not_79_out, not_80_out, not_81_out, INPUT[9], not_82_out, INPUT[11]);
  and and_10 (MOVCA_2, not_83_out, INPUT[1], not_84_out, not_85_out, not_86_out, not_87_out, not_88_out, not_89_out, not_90_out, INPUT[9], not_91_out, INPUT[11]);
  and and_11 (MOVCB_1, not_92_out, not_93_out, INPUT[2], INPUT[3], not_94_out, not_95_out, not_96_out, not_97_out, not_98_out, INPUT[9], INPUT[10], not_99_out);
  and and_12 (MOVCB_2, not_100_out, INPUT[1], not_101_out, not_102_out, not_103_out, not_104_out, not_105_out, not_106_out, not_107_out, INPUT[9], INPUT[10], not_108_out);
endmodule

module Instruction_sub (
  input  [11:0] INPUT,
  output ADDA_1,
  output ADDA_2,
  output ADDB_1,
  output ADDB_2
);

  wire not_1_out, not_2_out, not_3_out, not_4_out, not_5_out, not_6_out, not_7_out, not_8_out, not_9_out,
       not_10_out, not_11_out, not_12_out, not_13_out, not_14_out, not_15_out, not_16_out;

  not not_1 (not_1_out, INPUT[0]);
  not not_2 (not_2_out, INPUT[1]);
  not not_3 (not_3_out, INPUT[6]);
  not not_4 (not_4_out, INPUT[7]);
  not not_5 (not_5_out, INPUT[0]);
  not not_6 (not_6_out, INPUT[2]);
  not not_7 (not_7_out, INPUT[3]);
  not not_8 (not_8_out, INPUT[6]);
  not not_9 (not_9_out, INPUT[7]);
  not not_10 (not_10_out, INPUT[0]);
  not not_11 (not_11_out, INPUT[1]);
  not not_12 (not_12_out, INPUT[6]);
  not not_13 (not_13_out, INPUT[0]);
  not not_14 (not_14_out, INPUT[2]);
  not not_15 (not_15_out, INPUT[3]);
  not not_16 (not_16_out, INPUT[6]);
  and and_1 (ADDA_1, not_1_out, not_2_out, INPUT[2], INPUT[3], INPUT[4], INPUT[5], not_3_out, not_4_out, INPUT[8], INPUT[9], INPUT[10], INPUT[11]);
  and and_2 (ADDA_2, not_5_out, INPUT[1], not_6_out, not_7_out, INPUT[4], INPUT[5], not_8_out, not_9_out, INPUT[8], INPUT[9], INPUT[10], INPUT[11]);
  and and_3 (ADDB_1, not_10_out, not_11_out, INPUT[2], INPUT[3], INPUT[4], INPUT[5], not_12_out, INPUT[7], INPUT[8], INPUT[9], INPUT[10], INPUT[11]);
  and and_4 (ADDB_2, not_13_out, INPUT[1], not_14_out, not_15_out, INPUT[4], INPUT[5], not_16_out, INPUT[7], INPUT[8], INPUT[9], INPUT[10], INPUT[11]);
endmodule

module Instruction_AND_OR_XOR (
  input  [11:0] INPUT,
  output ANDA_C,
  output ANDA_C_2,
  output ANDA_B,
  output ANDA_B_2,
  output ORA_C,
  output ORA_C_2,
  output ORA_B,
  output ORA_B_2,
  output XORA_C,
  output XORA_C_2,
  output XORA_B,
  output XORA_B_2
);

  wire not_1_out, not_2_out, not_3_out, not_4_out, not_5_out, not_6_out, not_7_out, not_8_out, not_9_out,
       not_10_out, not_11_out, not_12_out, not_13_out, not_14_out, not_15_out, not_16_out, not_17_out,
       not_18_out, not_19_out, not_20_out, not_21_out, not_22_out, not_23_out, not_24_out, not_25_out,
       not_26_out, not_27_out, not_28_out, not_29_out, not_30_out, not_31_out, not_32_out, not_33_out,
       not_34_out, not_35_out, not_36_out, not_37_out, not_38_out, not_39_out, not_40_out, not_41_out,
       not_42_out, not_43_out, not_44_out, not_45_out, not_46_out, not_47_out, not_48_out;

  not not_1 (not_1_out, INPUT[0]);
  not not_2 (not_2_out, INPUT[1]);
  not not_3 (not_3_out, INPUT[11]);
  not not_4 (not_4_out, INPUT[0]);
  not not_5 (not_5_out, INPUT[2]);
  not not_6 (not_6_out, INPUT[3]);
  not not_7 (not_7_out, INPUT[11]);
  not not_8 (not_8_out, INPUT[0]);
  not not_9 (not_9_out, INPUT[1]);
  not not_10 (not_10_out, INPUT[10]);
  not not_11 (not_11_out, INPUT[0]);
  not not_12 (not_12_out, INPUT[2]);
  not not_13 (not_13_out, INPUT[3]);
  not not_14 (not_14_out, INPUT[10]);
  not not_15 (not_15_out, INPUT[0]);
  not not_16 (not_16_out, INPUT[1]);
  not not_17 (not_17_out, INPUT[10]);
  not not_18 (not_18_out, INPUT[11]);
  not not_19 (not_19_out, INPUT[0]);
  not not_20 (not_20_out, INPUT[2]);
  not not_21 (not_21_out, INPUT[3]);
  not not_22 (not_22_out, INPUT[10]);
  not not_23 (not_23_out, INPUT[11]);
  not not_24 (not_24_out, INPUT[0]);
  not not_25 (not_25_out, INPUT[1]);
  not not_26 (not_26_out, INPUT[9]);
  not not_27 (not_27_out, INPUT[0]);
  not not_28 (not_28_out, INPUT[2]);
  not not_29 (not_29_out, INPUT[3]);
  not not_30 (not_30_out, INPUT[9]);
  not not_31 (not_31_out, INPUT[0]);
  not not_32 (not_32_out, INPUT[1]);
  not not_33 (not_33_out, INPUT[9]);
  not not_34 (not_34_out, INPUT[10]);
  not not_35 (not_35_out, INPUT[0]);
  not not_36 (not_36_out, INPUT[2]);
  not not_37 (not_37_out, INPUT[3]);
  not not_38 (not_38_out, INPUT[9]);
  not not_39 (not_39_out, INPUT[10]);
  not not_40 (not_40_out, INPUT[0]);
  not not_41 (not_41_out, INPUT[1]);
  not not_42 (not_42_out, INPUT[9]);
  not not_43 (not_43_out, INPUT[11]);
  not not_44 (not_44_out, INPUT[0]);
  not not_45 (not_45_out, INPUT[2]);
  not not_46 (not_46_out, INPUT[3]);
  not not_47 (not_47_out, INPUT[9]);
  not not_48 (not_48_out, INPUT[11]);
  and and_1 (ANDA_C, not_1_out, not_2_out, INPUT[2], INPUT[3], INPUT[4], INPUT[5], INPUT[6], INPUT[7], INPUT[8], INPUT[9], INPUT[10], not_3_out);
  and and_2 (ANDA_C_2, not_4_out, INPUT[1], not_5_out, not_6_out, INPUT[4], INPUT[5], INPUT[6], INPUT[7], INPUT[8], INPUT[9], INPUT[10], not_7_out);
  and and_3 (ANDA_B, not_8_out, not_9_out, INPUT[2], INPUT[3], INPUT[4], INPUT[5], INPUT[6], INPUT[7], INPUT[8], INPUT[9], not_10_out, INPUT[11]);
  and and_4 (ANDA_B_2, not_11_out, INPUT[1], not_12_out, not_13_out, INPUT[4], INPUT[5], INPUT[6], INPUT[7], INPUT[8], INPUT[9], not_14_out, INPUT[11]);
  and and_5 (ORA_C, not_15_out, not_16_out, INPUT[2], INPUT[3], INPUT[4], INPUT[5], INPUT[6], INPUT[7], INPUT[8], INPUT[9], not_17_out, not_18_out);
  and and_6 (ORA_C_2, not_19_out, INPUT[1], not_20_out, not_21_out, INPUT[4], INPUT[5], INPUT[6], INPUT[7], INPUT[8], INPUT[9], not_22_out, not_23_out);
  and and_7 (ORA_B, not_24_out, not_25_out, INPUT[2], INPUT[3], INPUT[4], INPUT[5], INPUT[6], INPUT[7], INPUT[8], not_26_out, INPUT[10], INPUT[11]);
  and and_8 (ORA_B_2, not_27_out, INPUT[1], not_28_out, not_29_out, INPUT[4], INPUT[5], INPUT[6], INPUT[7], INPUT[8], not_30_out, INPUT[10], INPUT[11]);
  and and_9 (XORA_C, not_31_out, not_32_out, INPUT[2], INPUT[3], INPUT[4], INPUT[5], INPUT[6], INPUT[7], INPUT[8], not_33_out, not_34_out, INPUT[11]);
  and and_10 (XORA_C_2, not_35_out, INPUT[1], not_36_out, not_37_out, INPUT[4], INPUT[5], INPUT[6], INPUT[7], INPUT[8], not_38_out, not_39_out, INPUT[11]);
  and and_11 (XORA_B, not_40_out, not_41_out, INPUT[2], INPUT[3], INPUT[4], INPUT[5], INPUT[6], INPUT[7], INPUT[8], not_42_out, INPUT[10], not_43_out);
  and and_12 (XORA_B_2, not_44_out, INPUT[1], not_45_out, not_46_out, INPUT[4], INPUT[5], INPUT[6], INPUT[7], INPUT[8], not_47_out, INPUT[10], not_48_out);
endmodule

module Instruction_LDA_STA (
  input  [11:0] INPUT,
  output LDA_1,
  output LDA_2,
  output LDA_3,
  output LDA_4,
  output LDA_5,
  output LDA_6,
  output STA_1,
  output STA_2,
  output STA_3,
  output STA_4,
  output STA_5,
  output STA_6
);

  wire not_1_out, not_2_out, not_3_out, not_4_out, not_5_out, not_6_out, not_7_out, not_8_out, not_9_out,
       not_10_out, not_11_out, not_12_out, not_13_out, not_14_out, not_15_out, not_16_out, not_17_out,
       not_18_out, not_19_out, not_20_out, not_21_out, not_22_out, not_23_out, not_24_out, not_25_out,
       not_26_out, not_27_out, not_28_out, not_29_out, not_30_out, not_31_out, not_32_out, not_33_out,
       not_34_out, not_35_out, not_36_out, not_37_out, not_38_out, not_39_out, not_40_out, not_41_out,
       not_42_out, not_43_out, not_44_out, not_45_out, not_46_out, not_47_out, not_48_out, not_49_out,
       not_50_out, not_51_out, not_52_out, not_53_out, not_54_out, not_55_out, not_56_out, not_57_out,
       not_58_out, not_59_out, not_60_out, not_61_out, not_62_out, not_63_out, not_64_out, not_65_out,
       not_66_out, not_67_out, not_68_out, not_69_out, not_70_out, not_71_out, not_72_out, not_73_out,
       not_74_out;

  not not_1 (not_1_out, INPUT[0]);
  not not_2 (not_2_out, INPUT[1]);
  not not_3 (not_3_out, INPUT[5]);
  not not_4 (not_4_out, INPUT[7]);
  not not_5 (not_5_out, INPUT[9]);
  not not_6 (not_6_out, INPUT[11]);
  not not_7 (not_7_out, INPUT[0]);
  not not_8 (not_8_out, INPUT[2]);
  not not_9 (not_9_out, INPUT[3]);
  not not_10 (not_10_out, INPUT[5]);
  not not_11 (not_11_out, INPUT[7]);
  not not_12 (not_12_out, INPUT[9]);
  not not_13 (not_13_out, INPUT[11]);
  not not_14 (not_14_out, INPUT[0]);
  not not_15 (not_15_out, INPUT[2]);
  not not_16 (not_16_out, INPUT[5]);
  not not_17 (not_17_out, INPUT[7]);
  not not_18 (not_18_out, INPUT[9]);
  not not_19 (not_19_out, INPUT[11]);
  not not_20 (not_20_out, INPUT[0]);
  not not_21 (not_21_out, INPUT[3]);
  not not_22 (not_22_out, INPUT[5]);
  not not_23 (not_23_out, INPUT[7]);
  not not_24 (not_24_out, INPUT[9]);
  not not_25 (not_25_out, INPUT[11]);
  not not_26 (not_26_out, INPUT[0]);
  not not_27 (not_27_out, INPUT[5]);
  not not_28 (not_28_out, INPUT[7]);
  not not_29 (not_29_out, INPUT[9]);
  not not_30 (not_30_out, INPUT[11]);
  not not_31 (not_31_out, INPUT[1]);
  not not_32 (not_32_out, INPUT[2]);
  not not_33 (not_33_out, INPUT[3]);
  not not_34 (not_34_out, INPUT[5]);
  not not_35 (not_35_out, INPUT[7]);
  not not_36 (not_36_out, INPUT[9]);
  not not_37 (not_37_out, INPUT[11]);
  not not_38 (not_38_out, INPUT[0]);
  not not_39 (not_39_out, INPUT[1]);
  not not_40 (not_40_out, INPUT[4]);
  not not_41 (not_41_out, INPUT[6]);
  not not_42 (not_42_out, INPUT[8]);
  not not_43 (not_43_out, INPUT[10]);
  not not_44 (not_44_out, INPUT[0]);
  not not_45 (not_45_out, INPUT[2]);
  not not_46 (not_46_out, INPUT[3]);
  not not_47 (not_47_out, INPUT[4]);
  not not_48 (not_48_out, INPUT[6]);
  not not_49 (not_49_out, INPUT[8]);
  not not_50 (not_50_out, INPUT[10]);
  not not_51 (not_51_out, INPUT[0]);
  not not_52 (not_52_out, INPUT[2]);
  not not_53 (not_53_out, INPUT[4]);
  not not_54 (not_54_out, INPUT[6]);
  not not_55 (not_55_out, INPUT[8]);
  not not_56 (not_56_out, INPUT[10]);
  not not_57 (not_57_out, INPUT[0]);
  not not_58 (not_58_out, INPUT[3]);
  not not_59 (not_59_out, INPUT[4]);
  not not_60 (not_60_out, INPUT[6]);
  not not_61 (not_61_out, INPUT[8]);
  not not_62 (not_62_out, INPUT[10]);
  not not_63 (not_63_out, INPUT[0]);
  not not_64 (not_64_out, INPUT[4]);
  not not_65 (not_65_out, INPUT[6]);
  not not_66 (not_66_out, INPUT[8]);
  not not_67 (not_67_out, INPUT[10]);
  not not_68 (not_68_out, INPUT[1]);
  not not_69 (not_69_out, INPUT[2]);
  not not_70 (not_70_out, INPUT[3]);
  not not_71 (not_71_out, INPUT[4]);
  not not_72 (not_72_out, INPUT[6]);
  not not_73 (not_73_out, INPUT[8]);
  not not_74 (not_74_out, INPUT[10]);
  and and_1 (LDA_1, not_1_out, not_2_out, INPUT[2], INPUT[3], INPUT[4], not_3_out, INPUT[6], not_4_out, INPUT[8], not_5_out, INPUT[10], not_6_out);
  and and_2 (LDA_2, not_7_out, INPUT[1], not_8_out, not_9_out, INPUT[4], not_10_out, INPUT[6], not_11_out, INPUT[8], not_12_out, INPUT[10], not_13_out);
  and and_3 (LDA_3, not_14_out, INPUT[1], not_15_out, INPUT[3], INPUT[4], not_16_out, INPUT[6], not_17_out, INPUT[8], not_18_out, INPUT[10], not_19_out);
  and and_4 (LDA_4, not_20_out, INPUT[1], INPUT[2], not_21_out, INPUT[4], not_22_out, INPUT[6], not_23_out, INPUT[8], not_24_out, INPUT[10], not_25_out);
  and and_5 (LDA_5, not_26_out, INPUT[1], INPUT[2], INPUT[3], INPUT[4], not_27_out, INPUT[6], not_28_out, INPUT[8], not_29_out, INPUT[10], not_30_out);
  and and_6 (LDA_6, INPUT[0], not_31_out, not_32_out, not_33_out, INPUT[4], not_34_out, INPUT[6], not_35_out, INPUT[8], not_36_out, INPUT[10], not_37_out);
  and and_7 (STA_1, not_38_out, not_39_out, INPUT[2], INPUT[3], not_40_out, INPUT[5], not_41_out, INPUT[7], not_42_out, INPUT[9], not_43_out, INPUT[11]);
  and and_8 (STA_2, not_44_out, INPUT[1], not_45_out, not_46_out, not_47_out, INPUT[5], not_48_out, INPUT[7], not_49_out, INPUT[9], not_50_out, INPUT[11]);
  and and_9 (STA_3, not_51_out, INPUT[1], not_52_out, INPUT[3], not_53_out, INPUT[5], not_54_out, INPUT[7], not_55_out, INPUT[9], not_56_out, INPUT[11]);
  and and_10 (STA_4, not_57_out, INPUT[1], INPUT[2], not_58_out, not_59_out, INPUT[5], not_60_out, INPUT[7], not_61_out, INPUT[9], not_62_out, INPUT[11]);
  and and_11 (STA_5, not_63_out, INPUT[1], INPUT[2], INPUT[3], not_64_out, INPUT[5], not_65_out, INPUT[7], not_66_out, INPUT[9], not_67_out, INPUT[11]);
  and and_12 (STA_6, INPUT[0], not_68_out, not_69_out, not_70_out, not_71_out, INPUT[5], not_72_out, INPUT[7], not_73_out, INPUT[9], not_74_out, INPUT[11]);
endmodule

module Intruction_JMP_OUT_HLT (
  input  [11:0] INPUT,
  output OUT_1,
  output OUT_2,
  output HLT_1,
  output HLT_2,
  output JMP_1,
  output JMP_2,
  output JMP_3,
  output JMP_4
);

  wire not_1_out, not_2_out, not_3_out, not_4_out, not_5_out, not_6_out, not_7_out, not_8_out, not_9_out,
       not_10_out, not_11_out, not_12_out, not_13_out, not_14_out, not_15_out, not_16_out, not_17_out,
       not_18_out, not_19_out, not_20_out, not_21_out, not_22_out, not_23_out, not_24_out, not_25_out,
       not_26_out, not_27_out, not_28_out, not_29_out, not_30_out, not_31_out, not_32_out, not_33_out;

  not not_1 (not_1_out, INPUT[0]);
  not not_2 (not_2_out, INPUT[1]);
  not not_3 (not_3_out, INPUT[8]);
  not not_4 (not_4_out, INPUT[9]);
  not not_5 (not_5_out, INPUT[10]);
  not not_6 (not_6_out, INPUT[11]);
  not not_7 (not_7_out, INPUT[0]);
  not not_8 (not_8_out, INPUT[2]);
  not not_9 (not_9_out, INPUT[3]);
  not not_10 (not_10_out, INPUT[8]);
  not not_11 (not_11_out, INPUT[9]);
  not not_12 (not_12_out, INPUT[10]);
  not not_13 (not_13_out, INPUT[11]);
  not not_14 (not_14_out, INPUT[0]);
  not not_15 (not_15_out, INPUT[1]);
  not not_16 (not_16_out, INPUT[5]);
  not not_17 (not_17_out, INPUT[0]);
  not not_18 (not_18_out, INPUT[2]);
  not not_19 (not_19_out, INPUT[3]);
  not not_20 (not_20_out, INPUT[5]);
  not not_21 (not_21_out, INPUT[0]);
  not not_22 (not_22_out, INPUT[1]);
  not not_23 (not_23_out, INPUT[7]);
  not not_24 (not_24_out, INPUT[0]);
  not not_25 (not_25_out, INPUT[2]);
  not not_26 (not_26_out, INPUT[3]);
  not not_27 (not_27_out, INPUT[7]);
  not not_28 (not_28_out, INPUT[0]);
  not not_29 (not_29_out, INPUT[2]);
  not not_30 (not_30_out, INPUT[7]);
  not not_31 (not_31_out, INPUT[0]);
  not not_32 (not_32_out, INPUT[3]);
  not not_33 (not_33_out, INPUT[7]);
  and and_1 (OUT_1, not_1_out, not_2_out, INPUT[2], INPUT[3], INPUT[4], INPUT[5], INPUT[6], INPUT[7], not_3_out, not_4_out, not_5_out, not_6_out);
  and and_2 (OUT_2, not_7_out, INPUT[1], not_8_out, not_9_out, INPUT[4], INPUT[5], INPUT[6], INPUT[7], not_10_out, not_11_out, not_12_out, not_13_out);
  and and_3 (HLT_1, not_14_out, not_15_out, INPUT[2], INPUT[3], INPUT[4], not_16_out, INPUT[6], INPUT[7], INPUT[8], INPUT[9], INPUT[10], INPUT[11]);
  and and_4 (HLT_2, not_17_out, INPUT[1], not_18_out, not_19_out, INPUT[4], not_20_out, INPUT[6], INPUT[7], INPUT[8], INPUT[9], INPUT[10], INPUT[11]);
  and and_5 (JMP_1, not_21_out, not_22_out, INPUT[2], INPUT[3], INPUT[4], INPUT[5], INPUT[6], not_23_out, INPUT[8], INPUT[9], INPUT[10], INPUT[11]);
  and and_6 (JMP_2, not_24_out, INPUT[1], not_25_out, not_26_out, INPUT[4], INPUT[5], INPUT[6], not_27_out, INPUT[8], INPUT[9], INPUT[10], INPUT[11]);
  and and_7 (JMP_3, not_28_out, INPUT[1], not_29_out, INPUT[3], INPUT[4], INPUT[5], INPUT[6], not_30_out, INPUT[8], INPUT[9], INPUT[10], INPUT[11]);
  and and_8 (JMP_4, not_31_out, INPUT[1], INPUT[2], not_32_out, INPUT[4], INPUT[5], INPUT[6], not_33_out, INPUT[8], INPUT[9], INPUT[10], INPUT[11]);
endmodule

module Instruction_MVI (
  input  [11:0] INPUT,
  output MVIA_1,
  output MVIA_2,
  output MVIA_3,
  output MVIA_4
);

  wire not_1_out, not_2_out, not_3_out, not_4_out, not_5_out, not_6_out, not_7_out, not_8_out, not_9_out,
       not_10_out, not_11_out, not_12_out, not_13_out, not_14_out, not_15_out, not_16_out, not_17_out,
       not_18_out, not_19_out, not_20_out, not_21_out;

  not not_1 (not_1_out, INPUT[0]);
  not not_2 (not_2_out, INPUT[1]);
  not not_3 (not_3_out, INPUT[5]);
  not not_4 (not_4_out, INPUT[7]);
  not not_5 (not_5_out, INPUT[9]);
  not not_6 (not_6_out, INPUT[0]);
  not not_7 (not_7_out, INPUT[2]);
  not not_8 (not_8_out, INPUT[3]);
  not not_9 (not_9_out, INPUT[5]);
  not not_10 (not_10_out, INPUT[7]);
  not not_11 (not_11_out, INPUT[9]);
  not not_12 (not_12_out, INPUT[0]);
  not not_13 (not_13_out, INPUT[2]);
  not not_14 (not_14_out, INPUT[5]);
  not not_15 (not_15_out, INPUT[7]);
  not not_16 (not_16_out, INPUT[9]);
  not not_17 (not_17_out, INPUT[0]);
  not not_18 (not_18_out, INPUT[3]);
  not not_19 (not_19_out, INPUT[5]);
  not not_20 (not_20_out, INPUT[7]);
  not not_21 (not_21_out, INPUT[9]);
  and and_1 (MVIA_1, not_1_out, not_2_out, INPUT[2], INPUT[3], INPUT[4], not_3_out, INPUT[6], not_4_out, INPUT[8], not_5_out, INPUT[10], INPUT[11]);
  and and_2 (MVIA_2, not_6_out, INPUT[1], not_7_out, not_8_out, INPUT[4], not_9_out, INPUT[6], not_10_out, INPUT[8], not_11_out, INPUT[10], INPUT[11]);
  and and_3 (MVIA_3, not_12_out, INPUT[1], not_13_out, INPUT[3], INPUT[4], not_14_out, INPUT[6], not_15_out, INPUT[8], not_16_out, INPUT[10], INPUT[11]);
  and and_4 (MVIA_4, not_17_out, INPUT[1], INPUT[2], not_18_out, INPUT[4], not_19_out, INPUT[6], not_20_out, INPUT[8], not_21_out, INPUT[10], INPUT[11]);
endmodule

module Instruction_JZ_JC_JNZ (
  input  [7:0] FLAGS,
  input  [11:0] INPUT,
  output JZ_1,
  output JZ_2,
  output JZ_3,
  output JZ_4,
  output JNZ_1,
  output JNZ_2,
  output JNZ_3,
  output JNZ_4,
  output JC_1,
  output JC_2,
  output JC_3,
  output JC_4
);

  wire not_1_out, not_2_out, not_3_out, not_4_out, not_5_out, not_6_out, not_7_out, not_8_out, not_9_out,
       not_10_out, not_11_out, not_12_out, not_13_out, not_14_out, not_15_out, not_16_out, not_17_out,
       not_18_out, not_19_out, not_20_out, not_21_out, not_22_out, not_23_out, not_24_out, not_25_out,
       not_26_out, not_27_out, not_28_out, not_29_out, not_30_out, not_31_out, not_32_out, not_33_out,
       not_34_out, not_35_out, not_36_out, not_37_out, not_38_out, not_39_out, not_40_out, not_41_out,
       not_42_out, not_43_out, not_44_out, not_45_out, not_46_out, not_47_out, not_48_out, not_49_out,
       not_50_out, not_51_out, not_52_out, not_53_out, not_54_out, not_55_out, not_56_out;

  not not_1 (not_1_out, FLAGS[3]);
  not not_2 (not_2_out, INPUT[0]);
  not not_3 (not_3_out, INPUT[1]);
  not not_4 (not_4_out, INPUT[7]);
  not not_5 (not_5_out, INPUT[10]);
  not not_6 (not_6_out, INPUT[11]);
  not not_7 (not_7_out, INPUT[0]);
  not not_8 (not_8_out, INPUT[2]);
  not not_9 (not_9_out, INPUT[3]);
  not not_10 (not_10_out, INPUT[7]);
  not not_11 (not_11_out, INPUT[10]);
  not not_12 (not_12_out, INPUT[11]);
  not not_13 (not_13_out, INPUT[0]);
  not not_14 (not_14_out, INPUT[2]);
  not not_15 (not_15_out, INPUT[7]);
  not not_16 (not_16_out, INPUT[10]);
  not not_17 (not_17_out, INPUT[11]);
  not not_18 (not_18_out, INPUT[0]);
  not not_19 (not_19_out, INPUT[3]);
  not not_20 (not_20_out, INPUT[7]);
  not not_21 (not_21_out, INPUT[10]);
  not not_22 (not_22_out, INPUT[11]);
  not not_23 (not_23_out, INPUT[0]);
  not not_24 (not_24_out, INPUT[1]);
  not not_25 (not_25_out, INPUT[7]);
  not not_26 (not_26_out, INPUT[11]);
  not not_27 (not_27_out, INPUT[0]);
  not not_28 (not_28_out, INPUT[2]);
  not not_29 (not_29_out, INPUT[3]);
  not not_30 (not_30_out, INPUT[7]);
  not not_31 (not_31_out, INPUT[11]);
  not not_32 (not_32_out, INPUT[0]);
  not not_33 (not_33_out, INPUT[2]);
  not not_34 (not_34_out, INPUT[7]);
  not not_35 (not_35_out, INPUT[11]);
  not not_36 (not_36_out, INPUT[0]);
  not not_37 (not_37_out, INPUT[3]);
  not not_38 (not_38_out, INPUT[7]);
  not not_39 (not_39_out, INPUT[11]);
  not not_40 (not_40_out, INPUT[0]);
  not not_41 (not_41_out, INPUT[1]);
  not not_42 (not_42_out, INPUT[7]);
  not not_43 (not_43_out, INPUT[10]);
  not not_44 (not_44_out, INPUT[0]);
  not not_45 (not_45_out, INPUT[2]);
  not not_46 (not_46_out, INPUT[3]);
  not not_47 (not_47_out, INPUT[7]);
  not not_48 (not_48_out, INPUT[10]);
  not not_49 (not_49_out, INPUT[0]);
  not not_50 (not_50_out, INPUT[2]);
  not not_51 (not_51_out, INPUT[7]);
  not not_52 (not_52_out, INPUT[10]);
  not not_53 (not_53_out, INPUT[0]);
  not not_54 (not_54_out, INPUT[3]);
  not not_55 (not_55_out, INPUT[7]);
  not not_56 (not_56_out, INPUT[10]);
  and and_1 (JZ_1, not_2_out, not_3_out, INPUT[2], INPUT[3], INPUT[4], INPUT[5], INPUT[6], not_4_out, INPUT[8], INPUT[9], not_5_out, not_6_out);
  and and_2 (JZ_2, not_7_out, INPUT[1], not_8_out, not_9_out, INPUT[4], INPUT[5], FLAGS[3], INPUT[6], not_10_out, INPUT[8], INPUT[9], not_11_out, not_12_out);
  and and_3 (JZ_3, not_13_out, INPUT[1], not_14_out, INPUT[3], INPUT[4], INPUT[5], INPUT[6], not_15_out, INPUT[8], INPUT[9], not_16_out, not_17_out);
  and and_4 (JZ_4, not_18_out, INPUT[1], INPUT[2], not_19_out, INPUT[4], INPUT[5], FLAGS[3], INPUT[6], not_20_out, INPUT[8], INPUT[9], not_21_out, not_22_out);
  and and_5 (JNZ_1, not_23_out, not_24_out, INPUT[2], INPUT[3], INPUT[4], INPUT[5], INPUT[6], not_25_out, INPUT[8], INPUT[9], INPUT[10], not_26_out);
  and and_6 (JNZ_2, not_27_out, INPUT[1], not_28_out, not_29_out, INPUT[4], INPUT[5], not_1_out, INPUT[6], not_30_out, INPUT[8], INPUT[9], INPUT[10], not_31_out);
  and and_7 (JNZ_3, not_32_out, INPUT[1], not_33_out, INPUT[3], INPUT[4], INPUT[5], INPUT[6], not_34_out, INPUT[8], INPUT[9], INPUT[10], not_35_out);
  and and_8 (JNZ_4, not_36_out, INPUT[1], INPUT[2], not_37_out, INPUT[4], INPUT[5], not_1_out, INPUT[6], not_38_out, INPUT[8], INPUT[9], INPUT[10], not_39_out);
  and and_9 (JC_1, not_40_out, not_41_out, INPUT[2], INPUT[3], INPUT[4], INPUT[5], INPUT[6], not_42_out, INPUT[8], INPUT[9], not_43_out, INPUT[11]);
  and and_10 (JC_2, not_44_out, INPUT[1], not_45_out, not_46_out, INPUT[4], INPUT[5], FLAGS[6], INPUT[6], not_47_out, INPUT[8], INPUT[9], not_48_out, INPUT[11]);
  and and_11 (JC_3, not_49_out, INPUT[1], not_50_out, INPUT[3], INPUT[4], INPUT[5], INPUT[6], not_51_out, INPUT[8], INPUT[9], not_52_out, INPUT[11]);
  and and_12 (JC_4, not_53_out, INPUT[1], INPUT[2], not_54_out, INPUT[4], INPUT[5], FLAGS[6], INPUT[6], not_55_out, INPUT[8], INPUT[9], not_56_out, INPUT[11]);
endmodule

module Instruction_RST (
  input  [11:0] INPUT,
  output RST_1
);

  wire not_1_out, not_2_out, not_3_out, not_4_out, not_5_out;

  not not_1 (not_1_out, INPUT[0]);
  not not_2 (not_2_out, INPUT[1]);
  not not_3 (not_3_out, INPUT[8]);
  not not_4 (not_4_out, INPUT[9]);
  not not_5 (not_5_out, INPUT[10]);
  and and_1 (RST_1, not_1_out, not_2_out, INPUT[2], INPUT[3], INPUT[4], INPUT[5], INPUT[6], INPUT[7], not_3_out, not_4_out, not_5_out, INPUT[11]);
endmodule

module Binary_to_Bcd_CVTR (
  input  [7:0] in_1,
  output [3:0] out_2,
  output [3:0] out_3,
  output [3:0] out_4
);

  wire pull_resistor_1_node, pull_resistor_2_node, test_1_out_5, test_1_out_6, test_1_out_7, test_1_out_8,
       test_2_out_5, test_2_out_6, test_2_out_7, test_2_out_8, test_3_out_5, test_3_out_6, test_3_out_7,
       test_3_out_8, test_4_out_6, test_4_out_7, test_4_out_8, test_6_out_5, test_6_out_6, test_6_out_7,
       test_6_out_8;

  Pull_Resistor pull_resistor_1 (.node(pull_resistor_1_node));
  test test_1 (
    .out_8(test_1_out_8), .out_7(test_1_out_7), .out_6(test_1_out_6), .out_5(test_1_out_5), .in_1(in_1[5]),
    .in_2(in_1[6]), .in_3(in_1[7]), .in_4(pull_resistor_1_node));
  test test_2 (
    .out_8(test_2_out_8), .out_7(test_2_out_7), .out_6(test_2_out_6), .out_5(test_2_out_5), .in_1(in_1[4]),
    .in_2(test_1_out_8), .in_3(test_1_out_7), .in_4(test_1_out_6));
  Pull_Resistor pull_resistor_2 (.node(pull_resistor_2_node));
  test test_3 (
    .out_8(test_3_out_8), .out_7(test_3_out_7), .out_6(test_3_out_6), .out_5(test_3_out_5), .in_1(in_1[3]),
    .in_2(test_2_out_8), .in_3(test_2_out_7), .in_4(test_2_out_6));
  test test_4 (
    .out_8(test_4_out_8), .out_7(test_4_out_7), .out_6(test_4_out_6), .out_5(out_2[1]), .in_1(test_3_out_5),
    .in_2(test_2_out_5), .in_3(test_1_out_5), .in_4(pull_resistor_2_node));
  test test_5 (
    .out_8(out_3[1]), .out_7(out_3[2]), .out_6(out_3[3]), .out_5(out_2[0]), .in_1(test_6_out_5),
    .in_2(test_4_out_8), .in_3(test_4_out_7), .in_4(test_4_out_6));
  test test_6 (
    .out_8(test_6_out_8), .out_7(test_6_out_7), .out_6(test_6_out_6), .out_5(test_6_out_5), .in_1(in_1[2]),
    .in_2(test_3_out_8), .in_3(test_3_out_7), .in_4(test_3_out_6));
  test test_7 (
    .out_8(out_4[1]), .out_7(out_4[2]), .out_6(out_4[3]), .out_5(out_3[0]), .in_1(in_1[1]),
    .in_2(test_6_out_8), .in_3(test_6_out_7), .in_4(test_6_out_6));
  Pull_Resistor pull_resistor_3 (.node(out_2[3]));

  assign out_2[2] = out_2[3];
  assign out_4[0] = in_1[0];
endmodule
